# Fritzing sketch Sketch (saved by Fritzing 0.9.3b)

parts:
  Componente1 = Arduino Nano (Rev3.0)
  R1 = Resistor [tolerance=±5% resistance=220 package="1206 [SMD]"]
  S1 = Pushbutton [package="[SMD]"]

nets:
  N1: Componente1.GND, R1.Pin_0
  N2: Componente1.D4, R1.Pin_1, S1.Pin_1, S1.Pin_2
  N3: Componente1.5V, S1.Pin_3, S1.Pin_4

notes:
  To ARGB strip
